# Fritzing sketch dht-lipo-start (saved by Fritzing 0.9.3b)
circuit board: 8.46667cm x 5.64444cm
breadboards: 1

parts:
  Espessif_Serial_Wifi_Modul_1 = ESP8266 ESP01 [part_number=ESP8266 package=THT]
  DHT1 = DHT22 Humidity and Temperature Sensor
  U1 = LIPO-110mAh [package=lipo-110]

nets:
  GND: Espessif_Serial_Wifi_Modul_1.GND, DHT1.GND, U1.-
  VCC: Espessif_Serial_Wifi_Modul_1.VCC, DHT1.VDD, U1.+
  N1: Espessif_Serial_Wifi_Modul_1.GPIO02, DHT1.DATA

custom parts:
  ESP8266 ESP01: Generic WiFi Module based on the ESP8266 with onboard PCB antenna and UART communications
